# Fritzing sketch TVC_Nav_Com (saved by Fritzing 0.9.4)
circuit board: 8.46667cm x 5.64444cm
breadboards: 1

parts:
  Teensy1 = Teensy 3.6 (Basic)
  Part1 = Adafruit BNO055 STEMMA QT [part_number="Adafruit #4646"]
  Part2 = Adafruit BMP280 [part_number="Adafruit #2651"]
  Q1 = MOSFET-NCHANNEL [package=to220v]
  U1 = Voltage Regulator - 3.3V [package="TO220 [THT]"]
  X-Axis_Servo = Basic Servo [part_number=X-Axis]
  Y-Axis_Servo = Basic Servo [part_number=Y-Axis]
  BAT1 = BC9VPC [package=bc9vpc]
  R1 = Resistor [tolerance=±5% resistance=220 package="0805 [SMD]"]
  JP1 = Header 2 [package=screwterminal-3.5mm-2_lock]  # not connected

nets:
  GND: Teensy1.GND, Teensy1.GND1, Part1.GND, Part2.GND, Q1.S, U1.GND, X-Axis_Servo.gnd, Y-Axis_Servo.gnd, BAT1.V-, R1.Pin_1
  N1: Teensy1.D2, Y-Axis_Servo.pulse
  N2: Teensy1.D3, X-Axis_Servo.pulse
  N3: Teensy1.D6, Q1.G, R1.Pin_0
  N4: Teensy1.A4/D18, Part1.SCL, Part2.SDO/ADR
  N5: Teensy1.A5/D19, Part1.SDA, Part2.SCK/SCL
  3V3: Teensy1.3V3, Teensy1.3V3_1, Part2.VCC
  VCC: Teensy1.Vin, Part1.VCC, U1.output_voltage, X-Axis_Servo.vcc, Y-Axis_Servo.vcc
  N6: U1.input_voltage, BAT1.V+

custom parts:
  Teensy 3.6 (Basic): The Teensy is a complete USB-based microcontoller development system, in a very small footprint, capable of implementing many types of projects. All programming is done via the USB port. No special programmer is needed, only a standard micro-USB cable and a PC or Macintosh with a USB port.
  Adafruit BNO055 STEMMA QT: If you've ever ordered and wire up a 9-DOF sensor, chances are you've also realized the challenge of turning the sensor data from an accelerometer, gyroscope, and magnetometer into actual "3D space orientation"! Orientation is a hard problem to solve. The sensor fusion algorithms (the secret sauce that blends accelerometer, magnetometer, and gyroscope data into stable three-axis orientation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
  Adafruit BMP280: Bosch has stepped up their game with their new BMP280 sensor, an environmental sensor with temperature, barometric pressure that is the next generation upgrade to the BMP085/BMP180/BMP183. This sensor is great for all sorts of weather sensing and can even be used in both I2C and SPI! This precision sensor from Bosch is the best low-cost, precision sensing solution for measuring barometric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
